# Fritzing sketch raspi-vehicle (saved by Fritzing 1.0.1rc)

parts:
  Raspberry_Pi_Zero_2_W = Raspberry Pi Zero
  TB6612FNG_Motor_Driver = Motor Driver 1A Dual TB6612FNG
  Left_Motor = DC Motor [voltage_(max)=6V voltage_(min)=3V]
  Right_Motor = DC Motor [voltage_(max)=6V voltage_(min)=3V]
  4xAA_NiMH_Motor_Battery = Battery [voltage=4.8V]

nets:
  N1: Raspberry_Pi_Zero_2_W.pin_1, TB6612FNG_Motor_Driver.VCC, TB6612FNG_Motor_Driver.STBY
  N2: Raspberry_Pi_Zero_2_W.pin_6, TB6612FNG_Motor_Driver.GND, 4xAA_NiMH_Motor_Battery.-
  N3: Raspberry_Pi_Zero_2_W.pin_11, TB6612FNG_Motor_Driver.PWMA
  N4: Raspberry_Pi_Zero_2_W.pin_12, TB6612FNG_Motor_Driver.AIN1
  N5: Raspberry_Pi_Zero_2_W.pin_13, TB6612FNG_Motor_Driver.AIN2
  N6: Raspberry_Pi_Zero_2_W.pin_15, TB6612FNG_Motor_Driver.PWMB
  N7: Raspberry_Pi_Zero_2_W.pin_16, TB6612FNG_Motor_Driver.BIN1
  N8: Raspberry_Pi_Zero_2_W.pin_18, TB6612FNG_Motor_Driver.BIN2
  N9: TB6612FNG_Motor_Driver.B01, Right_Motor.pin_1
  N10: TB6612FNG_Motor_Driver.B02, Right_Motor.pin_2
  N11: TB6612FNG_Motor_Driver.A02, Left_Motor.pin_2
  N12: TB6612FNG_Motor_Driver.A01, Left_Motor.pin_1
  N13: TB6612FNG_Motor_Driver.VM, 4xAA_NiMH_Motor_Battery.+

notes:
  MOTOR OUTPUTS
  Yellow: AO1 -> left motor
  Green: AO2 -> left motor
  Blue: BO1 -> right motor
  Purple: BO2 -> right motor
  POWER
  Red: battery + -> VM
  Red: Pi pin 1 (3V3) -> VCC + STBY
  Black: battery - -> driver GND
  Black: Pi pin 6 -> common GND
  CONTROL SIGNALS
  Teal: pin 11 / GPIO17 -> PWMA
  Blue: pin 12 / GPIO18 -> AI1
  Purple: pin 13 / GPIO27 -> AI2
  Orange: pin 15 / GPIO22 -> PWMB
  Brown: pin 16 / GPIO23 -> BI1
  Gold: pin 18 / GPIO24 -> BI2
